# Fritzing sketch Sketch (saved by Fritzing 0.9.9b)

parts:
  Part2 = Arduino Mega Sensor Shield v2.0
  8_Channel_Relay1 = 8 Channel Power Relay
  8_Channel_Relay2 = 8 Channel Power Relay
  8_Channel_Relay3 = 8 Channel Power Relay
  8_Channel_Relay4 = 8 Channel Power Relay
  Part3 = IFR520 MOS module [package=THT]
  Mod1 = KY-019 5V Relay Module [package="Breakout board"]
  LED1 = LED - 5mm [color="Red (633nm)" current=0.030 package="5 mm [THT]"]
  12V = 12 battery [package=battery]
  9V = BC9VPC [package=bc9vpc]
  M1 = RioRand LM2596
  S1 = Taiway 100-SP-X-T1 SPDT Miniature Toggle Switch [part_number=100-SP-X-T1-0-0-B1-M1 package=THT]
  F1 = FUSE [package=fuse_5mm]

nets:
  N1: Part2.pin0, Part3.V+, LED1.anode
  N2: Part2.pin_48, Part2.pin_96, 8_Channel_Relay3.IN1
  N3: Part2.pin_49, Part2.pin_99, 8_Channel_Relay3.IN2
  N4: Part2.pin_50, Part2.pin_102, 8_Channel_Relay3.IN3
  N5: Part2.pin_51, Part2.pin_105, 8_Channel_Relay3.IN4
  N6: Part2.pin_52, Part2.pin_132, 8_Channel_Relay3.IN5
  N7: Part2.pin_53, Part2.pin_135, 8_Channel_Relay3.IN6
  N8: Part2.pin_54, Part2.pin_138, 8_Channel_Relay3.IN7
  N9: Part2.pin_55, Part2.pin_141, 8_Channel_Relay3.IN8
  N10: Part2.pin_56, Part2.pin_168, 8_Channel_Relay1.IN1
  N11: Part2.pin_57, Part2.pin_171, 8_Channel_Relay1.IN2
  N12: Part2.pin_58, Part2.pin_174, 8_Channel_Relay1.IN3
  N13: Part2.pin_59, Part2.pin_177, 8_Channel_Relay1.IN4
  N14: Part2.pin_60, Part2.pin_204, 8_Channel_Relay1.IN5
  N15: Part2.pin_61, Part2.pin_207, 8_Channel_Relay1.IN6
  N16: Part2.pin_62, Part2.pin_210, 8_Channel_Relay1.IN7
  N17: Part2.pin_63, Part2.pin_213, 8_Channel_Relay1.IN8
  N18: Part2.pin_64, Part2.pin_240, 8_Channel_Relay2.IN1
  N19: Part2.pin_65, Part2.pin_243, 8_Channel_Relay2.IN2
  N20: Part2.pin_66, Part2.pin_246, 8_Channel_Relay2.IN3
  N21: Part2.pin_67, Part2.pin_249, 8_Channel_Relay2.IN4
  N22: Part2.pin_68, Part2.pin_276, 8_Channel_Relay2.IN5
  N23: Part2.pin_69, Part2.pin_279, 8_Channel_Relay2.IN6
  N24: Part2.pin_70, Part2.pin_282, 8_Channel_Relay2.IN7
  N25: Part2.pin_71, Part2.pin_285, 8_Channel_Relay2.IN8
  N26: Part2.pin_72, Part2.pin_108, 8_Channel_Relay4.IN1
  N27: Part2.pin_73, Part2.pin_111, 8_Channel_Relay4.IN2
  N28: Part2.pin_74, Part2.pin_114, 8_Channel_Relay4.IN3
  N29: Part2.pin_75, Part2.pin_117, 8_Channel_Relay4.IN4
  N30: Part2.pin_76, Part2.pin_144, 8_Channel_Relay4.IN5
  N31: Part2.pin_77, Part2.pin_147, 8_Channel_Relay4.IN6
  N32: Part2.pin_78, Part2.pin_150, 8_Channel_Relay4.IN7
  N33: Part2.pin_79, Part2.pin_153, 8_Channel_Relay4.IN8
  GND: 8_Channel_Relay1.GND, 8_Channel_Relay2.GND, 8_Channel_Relay3.GND, 8_Channel_Relay4.GND, M1.Pin_4
  VCC: 8_Channel_Relay1.VCC, 8_Channel_Relay2.VCC, 8_Channel_Relay3.VCC, 8_Channel_Relay4.VCC, Part3.VCC, Part3.VIN, Mod1.+, Mod1.NO, M1.Pin_3
  N34: 8_Channel_Relay1.NC, 8_Channel_Relay2.NC, 8_Channel_Relay3.NC, 8_Channel_Relay4.NC, Part3.V-, Part3.GND, Mod1.-, LED1.cathode, 12V.-, 9V.V-, M1.Pin_2, F1.2
  N35: 8_Channel_Relay1.NO#23, 8_Channel_Relay2.NO, 8_Channel_Relay3.NO, 8_Channel_Relay4.NO, S1.L1
  N36: 8_Channel_Relay1.NO#26, 8_Channel_Relay1.NO#29, 8_Channel_Relay1.NO#32, 8_Channel_Relay1.NO#35, 8_Channel_Relay1.NO#38, 8_Channel_Relay1.NO#41, 8_Channel_Relay1.NO#44
  N37: 8_Channel_Relay2.COM, F1.1
  N38: Part3.SIG, Mod1.Common
  N39: 12V.+, S1.L2
  N40: 9V.V+, M1.Pin_1

notes:
  Remote Control Receiver
  5V Power
  Safety Switch
  E-Fuse Connection Example

custom parts:
  8 Channel Power Relay: An 8 channel power relay. The module operates at 5V.
  KY-019 5V Relay Module: KY-019 5V Relay module, used to control AC circuits. (Special thanks to vanepp for fixing the PCB holes and other errors)
  12 battery: 12V lead acid type battery, like the Husqvarna YTH2448 12V 35AH battery. This is the mini version 1/4 the size of the actual battery to be closer to typical breadboard parts (around 2in wide rathher than 7in). The pads in pcb are sized to accomidate up to 14ga wire (as these batterys will deliver high currents.)
